# Fritzing sketch tube-radio-FM (saved by Fritzing 0.9.3b)

parts:
  ProMini_3_3V = Arduino Pro Mini v13
  1K = Resistor [tolerance=±5% resistance=220 package=THT]
  1K_2 = Resistor [tolerance=±5% resistance=220 package=THT]
  NE555 = General purpose bipolar Timer [package=dil-08]
  1M = Resistor [tolerance=±5% resistance=220 package=THT]
  1M_2 = Resistor [tolerance=±5% resistance=220 package=THT]
  RDA5807M_RRD102 = RDA5807M-RRD102 [chip_label=IC package="DIP (Dual Inline) [THT]"]
  1N4004 = Schottky Diode [part_number=1N5817 package="300 mil [THT]"]
  1000uF = Capacitor Polarized [package=panasonic_c]

nets:
  N1: ProMini_3_3V.A4, RDA5807M_RRD102.DATA
  N2: ProMini_3_3V.A5, RDA5807M_RRD102.SCLK
  N3: ProMini_3_3V.RAW, 1N4004.cathode
  GND: ProMini_3_3V.GND, NE555.GND, RDA5807M_RRD102.GND, 1000uF.-
  VCC: ProMini_3_3V.VCC, NE555._RES, NE555.VCC+, 1M.Pin_1, RDA5807M_RRD102.VCC
  N4: ProMini_3_3V.D5_PWM, NE555.OUT
  N5: 1K.Pin_0, 1K_2.Pin_0
  N6: 1K.Pin_1, RDA5807M_RRD102.LOUT
  N7: 1K_2.Pin_1, RDA5807M_RRD102.ROUT
  N8: NE555.TRI, NE555.TRE, 1M_2.Pin_1
  N9: NE555.DIS, 1M.Pin_0, 1M_2.Pin_0
  N10: 1N4004.anode, 1000uF.+

notes:
  6.3VAC
  heater current
  common ground
  pick up
  amp input
  Variable Capacitor

custom parts:
  RDA5807M-RRD102: RRD102 board with RDA5807M chip and quartz
